# Fritzing sketch LevelMeter (saved by Fritzing 0.9.1b)
breadboards: 1

parts:
  Part2 = Arduino Uno (Rev3)  # not connected
  Part3 = Arduino Ethernet Shield (Rev3)
  HC-SR1 = HC-SR04
  DS1 = DS18B20 1-Wire Temperature Sensor Probe Cable
  R1 = Resistor [tolerance=±5% resistance=4.7k package="1206 [SMD]"]

nets:
  N1: Part3.D2, DS1.DQ, R1.Pin_1
  N2: Part3.PWM_D5, HC-SR1.Echo
  N3: Part3.PWM_D6, HC-SR1.Trig
  5V: Part3.5V, HC-SR1.VCC, DS1.VDD, R1.Pin_0
  GND: Part3.GND, HC-SR1.GND, DS1.shield
